// Logisim project 1901CS58.circ as structural Verilog: 8 circuits, main circuit main
module main (
  input  ENABLE,
  input  CLEAR
);

  wire CLOCK_out, CONTROLLER_alu_src1, CONTROLLER_aw, CONTROLLER_bw, CONTROLLER_dw, CONTROLLER_iw,
       CONTROLLER_m_read, CONTROLLER_m_write, CONTROLLER_mem2rf, CONTROLLER_pw, CONTROLLER_r_dst,
       CONTROLLER_resw, CONTROLLER_rf_write, n8_bit_cpu_1_z;
  wire [1:0] CONTROLLER_alu_op, CONTROLLER_alusrc2, CONTROLLER_pc_src;
  wire [3:0] n8_bit_cpu_1_op_code;
  wire [7:0] n8_bit_cpu_1_new_pc, PC_q;
  wire [15:0] rom_1_data;

  // Probe on CONTROLLER_pw
  Register PC (.D(n8_bit_cpu_1_new_pc), .en(CONTROLLER_pw), .Q(PC_q), .clk(CLOCK_out), .clr(CLEAR));
  Clock CLOCK (.out(CLOCK_out));
  ROM #(.dataWidth(16)) rom_1 (.addr(PC_q), .data(rom_1_data), .sel(ENABLE));
  CONTROLLER CONTROLLER (
    .OP_CODE(n8_bit_cpu_1_op_code), .Z(n8_bit_cpu_1_z), .ENABLE(ENABLE), .CLOCK(CLOCK_out), .CLEAR(CLEAR),
    .M_READ(CONTROLLER_m_read), .M_WRITE(CONTROLLER_m_write), .IW(CONTROLLER_iw), .DW(CONTROLLER_dw),
    .R_DST(CONTROLLER_r_dst), .MEM2RF(CONTROLLER_mem2rf), .RF_WRITE(CONTROLLER_rf_write), .AW(CONTROLLER_aw),
    .BW(CONTROLLER_bw), .ALU_src1(CONTROLLER_alu_src1), .ALUsrc2(CONTROLLER_alusrc2),
    .ALU_OP(CONTROLLER_alu_op), .ResW(CONTROLLER_resw), .PC_src(CONTROLLER_pc_src), .PW(CONTROLLER_pw));
  _8_BIT_CPU u_8_bit_cpu_1 (
    .PC(PC_q), .INSTRUCTION(rom_1_data), .M_READ(CONTROLLER_m_read), .M_WRITE(CONTROLLER_m_write),
    .IW(CONTROLLER_iw), .DW(CONTROLLER_dw), .R_DST(CONTROLLER_r_dst), .MEM2RF(CONTROLLER_mem2rf),
    .RF_WRITE(CONTROLLER_rf_write), .AW(CONTROLLER_aw), .BW(CONTROLLER_bw), .ALU_src1(CONTROLLER_alu_src1),
    .ALU_src2(CONTROLLER_alusrc2), .ALU_OP(CONTROLLER_alu_op), .Z(n8_bit_cpu_1_z), .ResW(CONTROLLER_resw),
    .PC_src(CONTROLLER_pc_src), .OP_CODE(n8_bit_cpu_1_op_code), .ENABLE(ENABLE), .CLOCK(CLOCK_out),
    .CLEAR(CLEAR), .NEW_PC(n8_bit_cpu_1_new_pc));

  // Notes on the sheet:
  //   8 BIT CPU
  //   INSTRUCTION MEMORY
endmodule

// CPU DATAPATH
module _8_BIT_CPU (
  input  [7:0] PC,
  input  ALU_src1,
  input  RF_WRITE,
  input  ResW,
  input  IW,
  input  [15:0] INSTRUCTION,
  input  AW,
  input  [1:0] ALU_src2,
  input  R_DST,
  input  BW,
  input  [1:0] ALU_OP,
  input  [1:0] PC_src,
  input  M_READ,
  input  M_WRITE,
  input  MEM2RF,
  input  DW,
  input  ENABLE,
  input  CLOCK,
  input  CLEAR,
  output [3:0] OP_CODE,
  output Z,
  output [7:0] NEW_PC
);

  wire [1:0] multiplexer_1_out;
  wire [3:0] IR_q;
  wire [7:0] A_q, B_q, DR_q, IR_q_2, multiplexer_2_out, multiplexer_3_out, multiplexer_4_out,
       n4_x_8_bit_register_file_1_r_data1, n4_x_8_bit_register_file_1_r_data2, n8_bit_alu_1_result,
       ram_1_data, RES_q;

  Register #(.width(16)) IR (.D(INSTRUCTION), .en(IW), .Q({OP_CODE, IR_q_2, IR_q}), .clk(CLOCK), .clr(CLEAR));
  RAM #(.bus("separate")) ram_1 (
    .addr(RES_q), .din(B_q), .data(ram_1_data), .str(M_WRITE), .sel(ENABLE), .clk(CLOCK), .ld(M_READ),
    .clr(CLEAR));
  Register DR (.D(ram_1_data), .en(DW), .Q(DR_q), .clk(CLOCK), .clr(CLEAR));
  Multiplexer #(.width(2), .disabled(0), .enable("false")) multiplexer_1 (
    .in0(IR_q_2[5:4]), .in1(IR_q_2[3:2]), .out(multiplexer_1_out), .sel(R_DST));
  _4_x_8_BIT_REGISTER_FILE u_4_x_8_bit_register_file_1 (
    .R_ADDR1(IR_q_2[7:6]), .R_ADDR2(IR_q_2[5:4]), .W_ADDR(multiplexer_1_out), .W_DATA(multiplexer_2_out),
    .R_W_Enable(RF_WRITE), .CLOCK(CLOCK), .CLEAR(CLEAR), .R_DATA1(n4_x_8_bit_register_file_1_r_data1),
    .R_DATA2(n4_x_8_bit_register_file_1_r_data2));
  Multiplexer #(.width(8), .disabled(0), .enable("false")) multiplexer_2 (
    .in0(RES_q), .in1(DR_q), .out(multiplexer_2_out), .sel(MEM2RF));
  Register A (.D(n4_x_8_bit_register_file_1_r_data1), .en(AW), .Q(A_q), .clk(CLOCK), .clr(CLEAR));
  Register B (.D(n4_x_8_bit_register_file_1_r_data2), .en(BW), .Q(B_q), .clk(CLOCK), .clr(CLEAR));
  Multiplexer #(.width(8), .disabled(0), .enable("false")) multiplexer_3 (
    .in0(PC), .in1(A_q), .out(multiplexer_3_out), .sel(ALU_src1));
  Multiplexer #(.select(2), .width(8), .disabled(0), .enable("false")) multiplexer_4 (
    .in0(B_q), .in1(8'h1), .in2({IR_q_2[3:0], IR_q}), .in3({IR_q_2[3:0], IR_q}), .out(multiplexer_4_out),
    .sel(ALU_src2));
  _8_BIT_ALU u_8_bit_alu_1 (
    .D1(multiplexer_3_out), .D2(multiplexer_4_out), .ALU_SEL(ALU_OP), .Z(Z), .RESULT(n8_bit_alu_1_result));
  Register RES (.D(n8_bit_alu_1_result), .en(ResW), .Q(RES_q), .clk(CLOCK), .clr(CLEAR));
  Multiplexer #(.select(2), .width(8), .disabled(0), .enable("false")) multiplexer_5 (
    .in0(RES_q), .in1(RES_q), .in2(n8_bit_alu_1_result), .in3(IR_q_2), .out(NEW_PC), .sel(PC_src));

  // Notes on the sheet:
  //   DATA MEMORY
  //   IR[15-12]
  //   IR[11-10]
  //   IR[9-8]
  //   IR[7-6]
  //   IR[7-0]
  //   IR[11-4]
  //   RES[7-0]
  //   REGISTER FILE
  //   CPU DATAPATH (MULTICYCLE)
  //   JUMP[7-0]
  //   RES[7-0]
  //   8 BIT ALU
endmodule

// RF
module _4_x_8_BIT_REGISTER_FILE (
  input  R_W_Enable,
  input  [1:0] R_ADDR1,
  input  [1:0] R_ADDR2,
  input  [1:0] W_ADDR,
  input  [7:0] W_DATA,
  input  CLOCK,
  input  CLEAR,
  output [7:0] R_DATA1,
  output [7:0] R_DATA2
);

  wire decoder_1_out0, decoder_1_out1, decoder_1_out2, decoder_1_out3;
  wire [7:0] register_1_q, register_2_q, register_3_q, register_4_q;

  Decoder #(.select(2), .disabled(0)) decoder_1 (
    .out0(decoder_1_out0), .out1(decoder_1_out1), .out2(decoder_1_out2), .out3(decoder_1_out3), .sel(W_ADDR),
    .en(R_W_Enable));
  Register register_1 (.D(W_DATA), .en(decoder_1_out0), .Q(register_1_q), .clk(CLOCK), .clr(CLEAR));
  Register register_2 (.D(W_DATA), .en(decoder_1_out1), .Q(register_2_q), .clk(CLOCK), .clr(CLEAR));
  Register register_3 (.D(W_DATA), .en(decoder_1_out2), .Q(register_3_q), .clk(CLOCK), .clr(CLEAR));
  Register register_4 (.D(W_DATA), .en(decoder_1_out3), .Q(register_4_q), .clk(CLOCK), .clr(CLEAR));
  Multiplexer #(.select(2), .width(8), .disabled(0), .enable("false")) multiplexer_1 (
    .in0(register_1_q), .in1(register_2_q), .in2(register_3_q), .in3(register_4_q), .out(R_DATA1),
    .sel(R_ADDR1));
  Multiplexer #(.select(2), .width(8), .disabled(0), .enable("false")) multiplexer_2 (
    .in0(register_1_q), .in1(register_2_q), .in2(register_3_q), .in3(register_4_q), .out(R_DATA2),
    .sel(R_ADDR2));

  // Notes on the sheet:
  //   4 X 8 REGISTER FILE
endmodule

module _8_BIT_ALU (
  input  [7:0] D1,
  input  [7:0] D2,
  input  [1:0] ALU_SEL,
  output Z,
  output [7:0] RESULT
);

  wire adder_1_cout, comparator_1_eq, comparator_1_gt, comparator_1_lt, subtractor_1_bout;
  wire [7:0] adder_1_out, and_1_out, subtractor_1_out, xor_1_out;

  Adder adder_1 (.a(D1), .b(D2), .out(adder_1_out), .cin(1'b0), .cout(adder_1_cout));
  // Probe on adder_1_cout
  assign and_1_out = D1 & D2;  // AND_Gate and_1, 8 bits wide
  Subtractor subtractor_1 (.a(D1), .b(D2), .out(subtractor_1_out), .bin(1'b0), .bout(subtractor_1_bout));
  // Probe on subtractor_1_bout
  assign xor_1_out = D1 ^ D2;  // XOR_Gate xor_1, 8 bits wide
  Multiplexer #(.select(2), .width(8), .disabled(0), .enable("false")) multiplexer_1 (
    .in0(adder_1_out), .in1(and_1_out), .in2(xor_1_out), .in3(subtractor_1_out), .out(RESULT), .sel(ALU_SEL));
  Comparator comparator_1 (.a(D1), .b(D2), .gt(comparator_1_gt), .eq(comparator_1_eq), .lt(comparator_1_lt));
  Multiplexer #(.select(2), .disabled(0), .enable("false")) multiplexer_2 (
    .in0(comparator_1_eq), .in1(comparator_1_eq), .in2(comparator_1_lt), .in3(comparator_1_gt), .out(Z),
    .sel(ALU_SEL));

  // Notes on the sheet:
  //   8 BIT ALU WITH COMPARATOR FOR BRANCH
endmodule

module TRANSITION_LOGIC (
  input  S3,
  input  S2,
  input  S1,
  input  S0,
  input  OP3,
  input  OP2,
  input  OP1,
  input  OP0,
  output N3,
  output N2,
  output N1,
  output N0
);

  wire and_1_out, and_2_out, and_3_out, and_4_out, and_5_out, and_6_out, and_7_out, and_8_out, and_9_out,
       and_10_out, and_11_out, and_12_out, and_13_out, and_14_out, and_15_out, not_1_out, not_2_out,
       not_3_out, not_4_out, not_5_out, not_6_out, not_7_out, not_8_out;

  not not_1 (not_1_out, S3);
  not not_2 (not_2_out, S2);
  not not_3 (not_3_out, S1);
  not not_4 (not_4_out, S0);
  not not_5 (not_5_out, OP3);
  not not_6 (not_6_out, OP2);
  not not_7 (not_7_out, OP1);
  not not_8 (not_8_out, OP0);
  and and_1 (and_1_out, not_1_out, not_2_out, not_3_out, S0, OP3, not_6_out);
  and and_2 (and_2_out, not_1_out, not_2_out, not_3_out, S0, OP3, OP1);
  and and_3 (and_3_out, not_1_out, S2, not_3_out, not_4_out, OP3);
  and and_4 (and_4_out, not_1_out, not_2_out, not_3_out, S0, not_5_out, OP2);
  and and_5 (and_5_out, not_1_out, not_2_out, not_3_out, S0, OP2, not_7_out);
  and and_6 (and_6_out, not_1_out, S2, not_4_out, not_5_out);
  and and_7 (and_7_out, not_1_out, S2, S1, not_4_out);
  and and_8 (and_8_out, not_1_out, not_2_out, not_3_out, S0, not_5_out, not_6_out);
  and and_9 (and_9_out, not_1_out, not_2_out, not_3_out, S0, OP3, OP2, OP1);
  and and_10 (and_10_out, not_1_out, S1, not_4_out);
  and and_11 (and_11_out, not_1_out, S2, not_4_out, not_5_out, not_7_out);
  and and_12 (and_12_out, not_1_out, not_2_out, not_4_out);
  and and_13 (and_13_out, not_1_out, not_2_out, not_3_out, OP3, not_6_out);
  and and_14 (and_14_out, not_1_out, not_4_out, not_5_out, OP1);
  and and_15 (and_15_out, not_1_out, S1, not_4_out);
  or or_1 (N3, and_1_out, and_2_out, and_3_out);
  or or_2 (N2, and_4_out, and_5_out, and_6_out, and_7_out);
  or or_3 (N1, and_8_out, and_9_out, and_10_out, and_11_out);
  or or_4 (N0, and_12_out, and_13_out, and_14_out, and_15_out);

  // Notes on the sheet:
  //   TRANSITION LOGIC
endmodule

module CONTROLLER (
  input  ENABLE,
  input  CLOCK,
  input  CLEAR,
  input  [3:0] OP_CODE,
  input  Z,
  output M_READ,
  output M_WRITE,
  output IW,
  output DW,
  output R_DST,
  output MEM2RF,
  output RF_WRITE,
  output AW,
  output BW,
  output ALU_src1,
  output [1:0] ALUsrc2,
  output [1:0] ALU_OP,
  output ResW,
  output [1:0] PC_src,
  output PW
);

  wire and_1_out, OUTPUT_LOGIC_alu_control, OUTPUT_LOGIC_pw, STATE_MEMORY_q0, STATE_MEMORY_q1,
       STATE_MEMORY_q2, STATE_MEMORY_q3, TRANSITION_LOGIC_n0, TRANSITION_LOGIC_n1, TRANSITION_LOGIC_n2,
       TRANSITION_LOGIC_n3;

  TRANSITION_LOGIC TRANSITION_LOGIC (
    .S3(STATE_MEMORY_q3), .S2(STATE_MEMORY_q2), .S1(STATE_MEMORY_q1), .S0(STATE_MEMORY_q0), .OP3(OP_CODE[3]),
    .OP2(OP_CODE[2]), .OP1(OP_CODE[1]), .OP0(OP_CODE[0]), .N3(TRANSITION_LOGIC_n3), .N2(TRANSITION_LOGIC_n2),
    .N1(TRANSITION_LOGIC_n1), .N0(TRANSITION_LOGIC_n0));
  Multiplexer #(.width(2), .disabled(0), .enable("false")) multiplexer_1 (
    .in0(2'b00), .in1(OP_CODE[1:0]), .out(ALU_OP), .sel(OUTPUT_LOGIC_alu_control));
  STATE_MEMORY STATE_MEMORY (
    .S3(TRANSITION_LOGIC_n3), .S2(TRANSITION_LOGIC_n2), .S1(TRANSITION_LOGIC_n1), .S0(TRANSITION_LOGIC_n0),
    .ENABLE(ENABLE), .CLOCK(CLOCK), .CLEAR(CLEAR), .Q3(STATE_MEMORY_q3), .Q2(STATE_MEMORY_q2),
    .Q1(STATE_MEMORY_q1), .Q0(STATE_MEMORY_q0));
  OUTPUT_LOGIC OUTPUT_LOGIC (
    .S3(STATE_MEMORY_q3), .S2(STATE_MEMORY_q2), .S1(STATE_MEMORY_q1), .S0(STATE_MEMORY_q0), .M_READ(M_READ),
    .M_WRITE(M_WRITE), .IW(IW), .DW(DW), .R_DST(R_DST), .MEM2RF(MEM2RF), .RF_WRITE(RF_WRITE), .AW(AW),
    .BW(BW), .ALU_src1(ALU_src1), .ALUsrc2(ALUsrc2), .ALU_Control(OUTPUT_LOGIC_alu_control), .ResW(ResW),
    .PC_src(PC_src), .PW(OUTPUT_LOGIC_pw));
  and and_1 (and_1_out, STATE_MEMORY_q3, ~STATE_MEMORY_q2, ~STATE_MEMORY_q1, STATE_MEMORY_q0);  // AND_Gate
  Multiplexer #(.disabled(0), .enable("false")) multiplexer_2 (
    .in0(OUTPUT_LOGIC_pw), .in1(Z), .out(PW), .sel(and_1_out));
  // Probe on OUTPUT_LOGIC_alu_control

  // Notes on the sheet:
  //   FSM (MOORE MACHINE)
  //   ALU CONTROL
  //   CONTROLLER
  //   BRANCH CONTROL
endmodule

module STATE_MEMORY (
  input  S3,
  input  S2,
  input  S1,
  input  S0,
  input  ENABLE,
  input  CLOCK,
  input  CLEAR,
  output Q3,
  output Q2,
  output Q1,
  output Q0
);

  Register #(.width(1)) register_1 (.D(S3), .en(ENABLE), .Q(Q3), .clk(CLOCK), .clr(CLEAR));
  Register #(.width(1)) register_2 (.D(S2), .en(ENABLE), .Q(Q2), .clk(CLOCK), .clr(CLEAR));
  Register #(.width(1)) register_3 (.D(S1), .en(ENABLE), .Q(Q1), .clk(CLOCK), .clr(CLEAR));
  Register #(.width(1)) register_4 (.D(S0), .en(ENABLE), .Q(Q0), .clk(CLOCK), .clr(CLEAR));

  // Notes on the sheet:
  //   STATE MEMORY
endmodule

module OUTPUT_LOGIC (
  input  S3,
  input  S2,
  input  S1,
  input  S0,
  output M_READ,
  output M_WRITE,
  output IW,
  output DW,
  output R_DST,
  output MEM2RF,
  output RF_WRITE,
  output AW,
  output BW,
  output ALU_src1,
  output [1:0] ALUsrc2,
  output ALU_Control,
  output ResW,
  output [1:0] PC_src,
  output PW
);

  wire and_6_out, and_7_out, and_10_out, and_11_out, and_12_out, and_13_out, and_14_out, and_15_out,
       and_16_out;

  and and_1 (M_READ, S2, S1, ~S0);  // AND_Gate
  and and_2 (M_WRITE, S2, ~S1, S0);  // AND_Gate
  and and_3 (IW, ~S3, ~S2, ~S1, ~S0);  // AND_Gate
  and and_4 (DW, S2, S1, ~S0);  // AND_Gate
  and and_5 (R_DST, ~S3, ~S2);  // AND_Gate
  and and_6 (and_6_out, S1, S0);
  and and_7 (and_7_out, S3, ~S1, ~S0);  // AND_Gate
  and and_8 (AW, ~S3, ~S2, ~S1, S0);  // AND_Gate
  or or_1 (ALU_src1, S3, S2, S1);
  and and_9 (ALUsrc2[0], ~S2, ~S1, ~S0);  // AND_Gate
  and and_10 (and_10_out, ~S3, S0);  // AND_Gate
  or or_2 (ALU_Control, S3, S1);
  and and_11 (and_11_out, S2, ~S1, ~S0);  // AND_Gate
  and and_12 (and_12_out, ~S3, ~S2, ~S1, S0);  // AND_Gate
  and and_13 (and_13_out, ~S3, ~S2, S1, ~S0);  // AND_Gate
  or or_3 (PC_src[1], ~S3, S1);  // OR_Gate
  and and_14 (and_14_out, ~S3, ~S2, ~S1, ~S0);  // AND_Gate
  and and_15 (and_15_out, S3, S0);
  and and_16 (and_16_out, S3, S1);
  or or_4 (RF_WRITE, and_6_out, and_7_out);
  or or_5 (ALUsrc2[1], S2, and_10_out);
  or or_6 (ResW, and_11_out, and_12_out, and_13_out);
  or or_7 (PW, and_14_out, and_15_out, and_16_out);

  assign BW = AW;
  assign MEM2RF = S2;
  assign PC_src[0] = S1;

  // Notes on the sheet:
  //   OUTPUT LOGIC
endmodule
